# Fritzing sketch To Be Decided Sketch (saved by Fritzing 0.9.4)
breadboards: 2

parts:
  Part1 = Arduino Uno (Rev3) - ICSP
  LCD2004-I2C1 = LCD2004-I2C
  LCD2004-I2C2 = LCD2004-I2C
  LCD2004-I2C3 = LCD2004-I2C
  LCD2004-I2C4 = LCD2004-I2C
  BUTTON1 = Arcade Button (yellow)
  BUTTON2 = Arcade Button (white)
  BUTTON3 = Arcade Button (red)
  BUTTON4 = Arcade Button (pink)
  BUTTON5 = Arcade Button (green)
  BUTTON6 = Arcade Button (blue)
  BUTTON7 = Arcade Button (yellow)
  BUTTON8 = Arcade Button (white)
  BUTTON9 = Arcade Button (red)
  BUTTON10 = Arcade Button (pink)
  BUTTON11 = Arcade Button (green)
  BUTTON12 = Arcade Button (blue)
  BUTTON13 = Arcade Button (yellow)
  BUTTON14 = Arcade Button (white)
  BUTTON15 = Arcade Button (red)
  BUTTON16 = Arcade Button (pink)
  Part2 = 24 NeoPixel Ring [part_number=1586]
  R1 = Resistor [tolerance=±5% resistance=220 package=THT]
  R2 = Resistor [tolerance=±5% resistance=220 package=THT]
  R3 = Resistor [tolerance=±5% resistance=220 package=THT]
  R4 = Resistor [tolerance=±5% resistance=220 package=THT]
  R5 = Resistor [tolerance=±5% resistance=220 package=THT]
  R6 = Resistor [tolerance=±5% resistance=220 package=THT]
  R7 = Resistor [tolerance=±5% resistance=220 package=THT]
  R8 = Resistor [tolerance=±5% resistance=220 package=THT]
  R9 = Resistor [tolerance=±5% resistance=220 package=THT]
  R10 = Resistor [tolerance=±5% resistance=220 package=THT]
  R11 = Resistor [tolerance=±5% resistance=220 package=THT]
  R12 = Resistor [tolerance=±5% resistance=220 package=THT]
  R13 = Resistor [tolerance=±5% resistance=220 package=THT]
  R14 = Resistor [tolerance=±5% resistance=220 package=THT]
  R15 = Resistor [tolerance=±5% resistance=220 package=THT]
  R16 = Resistor [tolerance=±5% resistance=220 package=THT]

nets:
  N1: Part1.A0, BUTTON14.no_name_yet#2, R15.Pin_0
  N2: Part1.A1, BUTTON13.no_name_yet#2, R16.Pin_0
  N3: Part1.A3, Part2.IN
  N4: Part1.A4/SDA, LCD2004-I2C1.SCL, LCD2004-I2C2.SCL, LCD2004-I2C3.SCL, LCD2004-I2C4.SCL
  N5: Part1.A5/SCL, LCD2004-I2C1.SDA, LCD2004-I2C2.SDA, LCD2004-I2C3.SDA, LCD2004-I2C4.SDA
  N6: Part1.ICSP_MOSI, Part1.D11_PWM/MOSI, BUTTON9.no_name_yet#2, R12.Pin_0
  N7: Part1.D8, BUTTON12.no_name_yet#2, R9.Pin_0
  N8: Part1.D9_PWM, BUTTON11.no_name_yet#2, R10.Pin_0
  N9: Part1.D10_PWM/SS, BUTTON10.no_name_yet#2, R11.Pin_0
  N10: Part1.D12/MISO, BUTTON16.no_name_yet#2, R13.Pin_0
  N11: Part1.D13/SCK, BUTTON15.no_name_yet#2, R14.Pin_0
  N12: Part1.D0/RX, BUTTON4.no_name_yet#2, R1.Pin_0
  N13: Part1.D1/TX, R2.Pin_0
  N14: Part1.D2, BUTTON2.no_name_yet#2, R3.Pin_0
  N15: Part1.D3_PWM, BUTTON1.no_name_yet#2, R4.Pin_0
  N16: Part1.D4, BUTTON8.no_name_yet#2, R5.Pin_0
  N17: Part1.D5_PWM, BUTTON7.no_name_yet#2, R6.Pin_0
  N18: Part1.D6_PWM, BUTTON6.no_name_yet#2, R7.Pin_0
  N19: Part1.D7, BUTTON5.no_name_yet#2, R8.Pin_0
  VCC: Part1.5V, LCD2004-I2C1.VCC, LCD2004-I2C2.VCC, LCD2004-I2C3.VCC, LCD2004-I2C4.VCC, BUTTON1.no_name_yet#1, BUTTON2.no_name_yet#1, BUTTON3.no_name_yet#1, BUTTON4.no_name_yet#1, BUTTON5.no_name_yet#1, BUTTON6.no_name_yet#1, BUTTON7.no_name_yet#1, BUTTON8.no_name_yet#1, BUTTON9.no_name_yet#1, BUTTON10.no_name_yet#1, BUTTON11.no_name_yet#1, BUTTON12.no_name_yet#1, BUTTON13.no_name_yet#1, BUTTON14.no_name_yet#1, BUTTON15.no_name_yet#1, BUTTON16.no_name_yet#1, Part2.VDD
  GND: Part1.GND, LCD2004-I2C1.GND, LCD2004-I2C2.GND, LCD2004-I2C3.GND, LCD2004-I2C4.GND, Part2.GND, R1.Pin_1, R2.Pin_1, R3.Pin_1, R4.Pin_1, R5.Pin_1, R6.Pin_1, R7.Pin_1, R8.Pin_1, R9.Pin_1, R10.Pin_1, R11.Pin_1, R12.Pin_1, R13.Pin_1, R14.Pin_1, R15.Pin_1, R16.Pin_1

custom parts:
  LCD2004-I2C: A standard character display with 4x20 characters. Comes in many colors with LCM2004 IIC attached.
  Arcade Button (yellow): Adafruit Arcade Button (yellow)
  Arcade Button (white): Adafruit Arcade Button (white)
  Arcade Button (red): Adafruit Arcade Button (red)
  Arcade Button (pink): Adafruit Arcade Button (pink)
  Arcade Button (green): Adafruit Arcade Button (green)
  Arcade Button (blue): Adafruit Arcade Button (blue)
  24 NeoPixel Ring: 24 ultra bright smart LED NeoPixels are arranged in a circle with 2.6" (66mm) outer diameter. The rings are 'chainable' - connect the output pin of one to the input pin of another. Use only one microcontroller pin to control as many as you can chain together! Each LED is addressable as the driver chip is inside the LED. Each one has ~18mA constant current drive so the color will be very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
